# Fritzing sketch MAIN (saved by Fritzing 0.9.3b)
circuit board: 8.58162cm x 5.39853cm
breadboards: 1

parts:
  Part1 = Arduino Uno (Rev3)
  IC1 = L293D [package=THT]
  TERMINAL-POWERSUPPLY = Screw terminal - 2 pins [package=THT]
  TERMINAL-MOTOR = Screw terminal - 2 pins [package=THT]
  125_kHz_RFID_module1 = RDM6300
  TERMINAL-ANTENNA1 = Screw terminal - 2 pins [package=THT]
  R1 = Resistor [tolerance=±5% resistance=10k package=THT]
  R2 = Resistor [tolerance=±5% resistance=10k package=THT]
  R3 = Resistor [tolerance=±5% resistance=10k package=THT]
  R4 = Resistor [tolerance=±5% resistance=10k package=THT]
  R5 = Resistor [tolerance=±5% resistance=10k package=THT]
  TERMINAL-LCD = screw terminal, 4 pins
  TERMINAL-SONIC = screw terminal, 4 pins
  TERMINAL-BUTTONS1 = screw terminal, 4 pins
  TERMINAL-WIRE = screw terminal, 3 pins

nets:
  N1: Part1.A4/SDA, TERMINAL-LCD.pin2
  N2: Part1.A5/SCL, TERMINAL-LCD.pin1
  N3: Part1.D8, IC1.In_2
  N4: Part1.D10_PWM/SS, R5.Pin_0, TERMINAL-BUTTONS1.pin4
  N5: Part1.D11_PWM/MOSI, R4.Pin_0, TERMINAL-BUTTONS1.pin3
  N6: Part1.D12/MISO, R3.Pin_0, TERMINAL-BUTTONS1.pin2
  N7: Part1.D13/SCK, IC1.In_1
  N8: Part1.GND, IC1.0V, TERMINAL-POWERSUPPLY.pin1, 125_kHz_RFID_module1.GND#60, R1.Pin_1, R2.Pin_1, R3.Pin_1, R4.Pin_1, R5.Pin_1, TERMINAL-LCD.pin4, TERMINAL-SONIC.pin4
  N9: Part1.D2, 125_kHz_RFID_module1.TX, 125_kHz_RFID_module1.GND#66, 125_kHz_RFID_module1.GND#67
  N10: Part1.D4, TERMINAL-SONIC.pin3
  N11: Part1.D5_PWM, TERMINAL-SONIC.pin2
  N12: Part1.D6_PWM, R2.Pin_0, TERMINAL-WIRE.pin3
  N13: Part1.D7, R1.Pin_0, TERMINAL-WIRE.pin2
  N14: Part1.5V, IC1.+V, 125_kHz_RFID_module1.+5V#61, TERMINAL-LCD.pin3, TERMINAL-SONIC.pin1, TERMINAL-BUTTONS1.pin1, TERMINAL-WIRE.pin1
  N15: IC1.Out_1_(_Controlled_by_Enable_1_), TERMINAL-MOTOR.pin1
  N16: IC1.Out_2_(_Controlled_by_Enable_1_), TERMINAL-MOTOR.pin2
  N17: IC1.+Vmotor, TERMINAL-POWERSUPPLY.pin2
  N18: 125_kHz_RFID_module1.ANT1, TERMINAL-ANTENNA1.pin1
  N19: 125_kHz_RFID_module1.ANT2, TERMINAL-ANTENNA1.pin2

custom parts:
  RDM6300: 125 kHz RFID module (serial interface)
