# Fritzing sketch MAIN_V2 (saved by Fritzing 0.9.3b)
circuit board: 8.02441cm x 7.14413cm
breadboards: 2

parts:
  IC1 = L293D [package=THT]
  125_kHz_RFID_module1 = RDM6300
  TERMINAL-ANTENNA1 = Screw terminal - 2 pins [package=THT]
  R1 = Resistor [tolerance=±5% resistance=10k package=THT]
  R2 = Resistor [tolerance=±5% resistance=10k package=THT]
  R3 = Resistor [tolerance=±5% resistance=10k package=THT]
  R4 = Resistor [tolerance=±5% resistance=10k package=THT]
  R5 = Resistor [tolerance=±5% resistance=10k package=THT]
  TERMINAL-LCD = screw terminal, 4 pins
  TERMINAL-SONIC = screw terminal, 4 pins
  TERMINAL-BUTTONS1 = screw terminal, 4 pins
  TERMINAL-WIRE = screw terminal, 3 pins
  TERMINAL-MOTOR&POWER = screw terminal, 4 pins
  Part2 = Arduino Nano (Rev3.0)
  SHARED-POWER = screw terminal, 3 pins

nets:
  N1: IC1.In_1, Part2.D13/SCK
  N2: IC1.Out_1_(_Controlled_by_Enable_1_), TERMINAL-MOTOR&POWER.pin1
  N3: IC1.0V, 125_kHz_RFID_module1.GND#60, R1.Pin_1, R2.Pin_1, R3.Pin_1, R4.Pin_1, R5.Pin_1, TERMINAL-LCD.pin1, TERMINAL-SONIC.pin1, TERMINAL-MOTOR&POWER.pin3, Part2.GND, SHARED-POWER.pin3
  N4: IC1.Out_2_(_Controlled_by_Enable_1_), TERMINAL-MOTOR&POWER.pin2
  N5: IC1.In_2, Part2.D8
  N6: IC1.+Vmotor, TERMINAL-MOTOR&POWER.pin4
  N7: IC1.+V, 125_kHz_RFID_module1.+5V#61, TERMINAL-LCD.pin4, TERMINAL-SONIC.pin4, TERMINAL-BUTTONS1.pin4, TERMINAL-WIRE.pin3, Part2.5V, SHARED-POWER.pin1
  N8: 125_kHz_RFID_module1.TX, 125_kHz_RFID_module1.GND#66, Part2.D2
  N9: 125_kHz_RFID_module1.ANT1, TERMINAL-ANTENNA1.pin1
  N10: 125_kHz_RFID_module1.ANT2, TERMINAL-ANTENNA1.pin2
  N11: R1.Pin_0, TERMINAL-WIRE.pin1, Part2.D7
  N12: R2.Pin_0, TERMINAL-WIRE.pin2, Part2.D6
  N13: R3.Pin_0, TERMINAL-BUTTONS1.pin1, Part2.D12/MISO
  N14: R4.Pin_0, TERMINAL-BUTTONS1.pin2, Part2.D11/MOSI
  N15: R5.Pin_0, TERMINAL-BUTTONS1.pin3, Part2.D10
  N16: TERMINAL-LCD.pin2, Part2.A5
  N17: TERMINAL-LCD.pin3, Part2.A4
  N18: TERMINAL-SONIC.pin2, Part2.D5
  N19: TERMINAL-SONIC.pin3, Part2.D4
  N20: Part2.VIN, SHARED-POWER.pin2

custom parts:
  RDM6300: 125 kHz RFID module (serial interface)
