# Fritzing sketch SONIC (saved by Fritzing 0.9.3b)
circuit board: 8.46667cm x 5.64444cm
stripboards: 1

parts:
  hc-sr2 = hc-sr04
  J1 = Screw terminal - 2 pins [package=THT]
  J2 = Screw terminal - 2 pins [package=THT]

nets:
  N1: hc-sr2.VCC, J1.pin1
  N2: hc-sr2.Trig, J1.pin2
  N3: hc-sr2.Echo, J2.pin1
  N4: hc-sr2.GND, J2.pin2
