# Fritzing sketch Projekt-2-PCB (saved by Fritzing 0.9.3b)
circuit board: 2.97979cm x 3.85737cm
circuit board: 4.64121cm x 3.15929cm
circuit board: 9.02069cm x 5.67412cm
breadboards: 1
perfboards: 3

parts:
  Part1 = Arduino Uno (Rev3)
  IC1 = L293D [package=THT]
  S1 = Pushbutton [package="[THT]"]
  S2 = Pushbutton [package="[THT]"]
  S3 = Pushbutton [package="[THT]"]
  R1 = Resistor [tolerance=±5% resistance=220 package=THT]
  R2 = Resistor [tolerance=±5% resistance=220 package=THT]
  R3 = Resistor [tolerance=±5% resistance=220 package=THT]
  R4 = Resistor [tolerance=±5% resistance=220 package=THT]
  R5 = Resistor [tolerance=±5% resistance=220 package=THT]
  S6 = Pushbutton [package="[THT]"]
  S7 = Pushbutton [package="[THT]"]
  TERMINAL-MECHANIC2 = Screw terminal - 2 pins [package=THT]
  TERMINAL-MECHANIC1 = Screw terminal - 2 pins [package=THT]
  TERMINAL-BUTTONS1 = Screw terminal - 2 pins [package=THT]
  TERMINAL-BUTTONS2 = Screw terminal - 2 pins [package=THT]
  TERMINAL-BUTTONS3 = Screw terminal - 2 pins [package=THT]
  TERMINAL-GENERAL = Screw terminal - 2 pins [package=THT]
  TERMINAL-MOTOR = Screw terminal - 2 pins [package=THT]
  TERMINAL-POWERSUPPLY = Screw terminal - 2 pins [package=THT]
  125_kHz_RFID_module1 = RDM6300
  TERMINAL-ANTENNA = Screw terminal - 2 pins [package=THT]
  TERMINAL-LCD2 = Screw terminal - 2 pins [package=THT]
  TERMINAL-LCD1 = Screw terminal - 2 pins [package=THT]
  TERMINAL-SONICUNIT1 = Screw terminal - 2 pins [package=THT]
  TERMINAL-SONICUNIT2 = Screw terminal - 2 pins [package=THT]
  hc-sr1 = hc-sr04
  TERMINAL-SONIC1 = Screw terminal - 2 pins [package=THT]
  TERMINAL-SONIC2 = Screw terminal - 2 pins [package=THT]

nets:
  N1: Part1.A4/SDA, TERMINAL-LCD1.pin2
  N2: Part1.A5/SCL, TERMINAL-LCD1.pin1
  N3: Part1.D8, IC1.In_2
  N4: Part1.D13/SCK, IC1.In_1
  N5: Part1.D2, 125_kHz_RFID_module1.TX, 125_kHz_RFID_module1.GND#66, 125_kHz_RFID_module1.GND#67
  N6: Part1.D4, TERMINAL-SONIC1.pin1
  N7: Part1.D5_PWM, TERMINAL-SONIC2.pin2
  N8: Part1.5V, IC1.+V, TERMINAL-GENERAL.pin2, 125_kHz_RFID_module1.+5V#61, TERMINAL-LCD2.pin1, TERMINAL-SONIC2.pin1
  N9: Part1.GND, IC1.0V, TERMINAL-GENERAL.pin1, TERMINAL-POWERSUPPLY.pin1, 125_kHz_RFID_module1.GND#60, TERMINAL-LCD2.pin2, TERMINAL-SONIC1.pin2
  N10: IC1.Out_1_(_Controlled_by_Enable_1_), TERMINAL-MOTOR.pin2
  N11: IC1.Out_2_(_Controlled_by_Enable_1_), TERMINAL-MOTOR.pin1
  N12: IC1.+Vmotor, TERMINAL-POWERSUPPLY.pin2
  N13: S1.Pin_1, S1.Pin_2
  N14: S1.Pin_3, S1.Pin_4, S2.Pin_3, S2.Pin_4, S3.Pin_3, S3.Pin_4, R1.Pin_1, R2.Pin_1, R3.Pin_1, TERMINAL-BUTTONS1.pin1, TERMINAL-BUTTONS1.pin2, TERMINAL-BUTTONS2.pin1, TERMINAL-BUTTONS2.pin2
  N15: S2.Pin_1, S2.Pin_2
  N16: S3.Pin_1, S3.Pin_2
  N17: R1.Pin_0, R2.Pin_0, R3.Pin_0, TERMINAL-BUTTONS3.pin1
  N18: R4.Pin_0, R5.Pin_0, TERMINAL-MECHANIC1.pin2
  N19: R4.Pin_1, R5.Pin_1, S6.Pin_3, S6.Pin_4, S7.Pin_3, S7.Pin_4, TERMINAL-MECHANIC2.pin1, TERMINAL-MECHANIC2.pin2, TERMINAL-MECHANIC1.pin1
  N20: S6.Pin_1, S6.Pin_2
  N21: S7.Pin_1, S7.Pin_2
  N22: 125_kHz_RFID_module1.ANT1, TERMINAL-ANTENNA.pin1
  N23: 125_kHz_RFID_module1.ANT2, TERMINAL-ANTENNA.pin2
  N24: TERMINAL-SONICUNIT1.pin1, hc-sr1.VCC
  N25: TERMINAL-SONICUNIT1.pin2, hc-sr1.Trig
  N26: TERMINAL-SONICUNIT2.pin1, hc-sr1.Echo
  N27: TERMINAL-SONICUNIT2.pin2, hc-sr1.GND

custom parts:
  RDM6300: 125 kHz RFID module (serial interface)
